// Logisim project comp1_design.circ as structural Verilog: 3 circuits, main circuit main
module main (
);

  wire button_1_out, clock_1_out, comparator_1_eq, d_ff_1_q, FF0_q, FF1_q, FF2_q, or_1_out,
       outputlogic_1_ew_g, outputlogic_1_ew_r, outputlogic_1_ew_y, outputlogic_1_ns_g, outputlogic_1_ns_r,
       outputlogic_1_ns_y, outputlogic_1_ped_w, statememory_1_d0, statememory_1_d1, statememory_1_d2;
  wire [3:0] counter_1_q;

  Counter #(.width(4), .max('hf)) counter_1 (
    .count(clock_1_out), .Q(counter_1_q), .clk(clock_1_out));  // open: load, D, carry, clr
  Button button_1 (.out(button_1_out));
  Clock clock_1 (.out(clock_1_out));
  or or_1 (or_1_out, button_1_out, d_ff_1_q);
  Comparator #(.width(4)) comparator_1 (.a(counter_1_q), .b(4'b1010), .eq(comparator_1_eq));  // open: gt, lt
  D_Flip_Flop d_ff_1 (
    .clk(clock_1_out), .D(or_1_out), .Q(d_ff_1_q), .reset(outputlogic_1_ped_w));  // open: Qn, preset, en
  D_Flip_Flop FF2 (.clk(clock_1_out), .D(statememory_1_d2), .Q(FF2_q));  // open: Qn, preset, en, reset
  D_Flip_Flop FF1 (.clk(clock_1_out), .D(statememory_1_d1), .Q(FF1_q));  // open: Qn, preset, en, reset
  D_Flip_Flop FF0 (.clk(clock_1_out), .D(statememory_1_d0), .Q(FF0_q));  // open: Qn, preset, en, reset
  OutputLogic outputlogic_1 (
    .Q2(FF2_q), .Q1(FF1_q), .Q0(FF0_q), .NS_G(outputlogic_1_ns_g), .NS_Y(outputlogic_1_ns_y),
    .NS_R(outputlogic_1_ns_r), .EW_G(outputlogic_1_ew_g), .EW_Y(outputlogic_1_ew_y),
    .EW_R(outputlogic_1_ew_r), .Ped_W(outputlogic_1_ped_w));
  StateMemory statememory_1 (
    .Q2(FF2_q), .Q1(FF1_q), .Q0(FF0_q), .T_Done(comparator_1_eq), .P_Latch(d_ff_1_q), .D2(statememory_1_d2),
    .D1(statememory_1_d1), .D0(statememory_1_d0));
  LED led_1 (.in(outputlogic_1_ns_r));
  LED led_2 (.in(outputlogic_1_ns_y));
  LED led_3 (.in(outputlogic_1_ns_g));
  LED led_4 (.in(outputlogic_1_ew_r));
  LED led_5 (.in(outputlogic_1_ew_y));
  LED led_6 (.in(outputlogic_1_ew_g));
  LED led_7 (.in(outputlogic_1_ped_w));
endmodule

module StateMemory (
  input  Q2,
  input  Q1,
  input  Q0,
  input  T_Done,
  input  P_Latch,
  output D2,
  output D1,
  output D0
);

  wire and_1_out, and_2_out, and_3_out, and_4_out, and_5_out, and_6_out, and_7_out, not_1_out, not_2_out,
       not_3_out, not_4_out, not_5_out, not_6_out, not_7_out, not_8_out, not_9_out, not_10_out, not_11_out,
       not_12_out, not_13_out, not_14_out;

  not not_1 (not_1_out, Q2);
  not not_2 (not_2_out, Q1);
  not not_3 (not_3_out, Q0);
  not not_4 (not_4_out, T_Done);
  not not_5 (not_5_out, Q2);
  not not_6 (not_6_out, Q1);
  not not_7 (not_7_out, Q2);
  not not_8 (not_8_out, Q0);
  not not_9 (not_9_out, Q2);
  not not_10 (not_10_out, T_Done);
  not not_11 (not_11_out, Q2);
  not not_12 (not_12_out, Q0);
  not not_13 (not_13_out, Q2);
  not not_14 (not_14_out, T_Done);
  and and_1 (and_1_out, not_1_out, Q1, Q0, T_Done, P_Latch);
  and and_2 (and_2_out, Q2, not_2_out, not_3_out, not_4_out);
  and and_3 (and_3_out, not_5_out, not_6_out, Q0, T_Done);
  and and_4 (and_4_out, not_7_out, Q1, not_8_out);
  and and_5 (and_5_out, not_9_out, Q1, not_10_out);
  and and_6 (and_6_out, not_11_out, not_12_out, T_Done);
  and and_7 (and_7_out, not_13_out, Q0, not_14_out);
  or or_1 (D2, and_1_out, and_2_out);
  or or_2 (D1, and_3_out, and_4_out, and_5_out);
  or or_3 (D0, and_6_out, and_7_out);
endmodule

module OutputLogic (
  input  Q2,
  input  Q1,
  input  Q0,
  output NS_G,
  output NS_Y,
  output NS_R,
  output EW_G,
  output EW_Y,
  output EW_R,
  output Ped_W
);

  wire not_1_out, not_2_out, not_3_out, not_4_out, not_5_out, not_6_out, not_7_out, not_8_out, not_9_out,
       not_10_out, not_11_out;

  not not_1 (not_1_out, Q2);
  not not_2 (not_2_out, Q1);
  not not_3 (not_3_out, Q0);
  not not_4 (not_4_out, Q2);
  not not_5 (not_5_out, Q1);
  or or_1 (NS_R, Q1, Q2);
  not not_6 (not_6_out, Q2);
  not not_7 (not_7_out, Q0);
  not not_8 (not_8_out, Q2);
  not not_9 (not_9_out, Q1);
  not not_10 (not_10_out, Q1);
  not not_11 (not_11_out, Q0);
  and and_1 (NS_G, not_1_out, not_2_out, not_3_out);
  and and_2 (NS_Y, not_4_out, not_5_out, Q0);
  and and_3 (EW_G, not_6_out, Q1, not_7_out);
  and and_4 (EW_Y, not_8_out, Q1, Q0);
  or or_2 (EW_R, not_9_out, Q2);
  and and_5 (Ped_W, Q2, not_10_out, not_11_out);
endmodule
